# Fritzing sketch RangeFinder (saved by Fritzing 0.9.3b)
breadboards: 1

parts:
  Part1 = Arduino Uno (Rev3)
  hc-sr1 = hc-sr04  # not connected
  R1 = Resistor [tolerance=±5% resistance=220 package=THT]
  R2 = Resistor [tolerance=±10% resistance=220 package=THT]
  LED1 = LED - 5mm [color="Red (633nm)" package="5 mm [THT]"]
  LED2 = LED - 5mm [color="Blue (430nm)" package="5 mm [THT]"]

nets:
  N1: Part1.D11_PWM/MOSI, LED1.anode
  N2: Part1.D13/SCK, LED2.anode
  N3: Part1.GND, R1.Pin_1, R2.Pin_1
  N4: R1.Pin_0, LED1.cathode
  N5: R2.Pin_0, LED2.cathode
